# Fritzing sketch pushbullet (saved by Fritzing 0.9.1b)
breadboards: 1

parts:
  U1 = ESP8266 WiFi Module [part_number=ESP8266]
  Part2 = Arduino Nano (Rev3.0)
  Part3 = FTDI Basic Programmer
  Part4 = Logic Level Converter
  PIR1 = PIR sensor

nets:
  N1: U1.RXD, Part4.RX_LV
  VCC: U1.VCC, Part2.3V3, Part4.LV
  N2: U1.CH_PD, Part4.RX2_LV
  GND: U1.GND, Part2.GND, Part4.GND, PIR1.GND
  N3: U1.TXD, Part4.TX_LV
  N4: Part2.D1/TX, Part4.RX_HV
  N5: Part2.D0/RX, Part4.TX_HV
  N6: Part2.D2, PIR1.SIG
  N7: Part2.D4, Part3.TXO
  N8: Part2.D5, Part3.RXI
  N9: Part2.D7, Part4.RX2_HV
  5V: Part2.5V, Part4.HV, PIR1.VDD

notes:
  Debug Serial

custom parts:
  ESP8266 WiFi Module: Generic WiFi Module based on the ESP8266 with onboard PCB antenna and UART communications
